# Fritzing sketch ddcs-expert-to-rrf (saved by Fritzing 0.9.3b)
circuit board: 7cm x 4.5cm
breadboards: 1

parts:
  R1 = Resistor [tolerance=±5% resistance=6.8 package=THT]
  Arduino_Pro_Micro = Arduino Pro Micro (Clone)
  PanelDue = JST XH 4A 2.54mm [package=THT]
  Controller = JST XH 4A 2.54mm [package=THT]
  DB15 = DB15 Connector [package=db15]
  R2 = Resistor [tolerance=±5% resistance=10k package=THT]

nets:
  N1: R1.Pin_0, Controller.pin1, R2.Pin_0
  N2: R1.Pin_1, Arduino_Pro_Micro.TXO
  N3: Arduino_Pro_Micro.RXI, PanelDue.pin1
  N4: Arduino_Pro_Micro.GND, PanelDue.pin3, Controller.pin3, DB15.8, DB15.9, R2.Pin_1
  N5: Arduino_Pro_Micro.D2, DB15.4
  N6: Arduino_Pro_Micro.D3, DB15.12
  N7: Arduino_Pro_Micro.D4, DB15.5
  N8: Arduino_Pro_Micro.D5, DB15.13
  N9: Arduino_Pro_Micro.D6, DB15.6
  N10: Arduino_Pro_Micro.D7, DB15.14
  N11: Arduino_Pro_Micro.D8, DB15.15
  N12: Arduino_Pro_Micro.D9, DB15.7
  N13: Arduino_Pro_Micro.D10, DB15.2
  N14: Arduino_Pro_Micro.D16, DB15.10
  N15: Arduino_Pro_Micro.D14, DB15.3
  N16: Arduino_Pro_Micro.D15, DB15.11
  N17: Arduino_Pro_Micro.VCC, PanelDue.pin4, Controller.pin4, DB15.1
  N18: PanelDue.pin2, Controller.pin2

custom parts:
  JST XH 4A 2.54mm: 4 Pin JST XH connector
  DB15 Connector: DB15 Connector Standard DB15 (D-Sub 15) pc midi or gameport connector. Can be used for old PC compatible joystic.
